// Logisim project lab2.circ as structural Verilog: 1 circuit, main circuit main
module main (
  input  A0,
  input  B1,
  input  B0
);

  // _3_to_8_decoder__74138 #(.Facing("east")) 3_to_8_decoder_74138_1: pin names not known; wires that end beside it: A0, B1, B0, 1'b1, 1'b0, 1'b0
endmodule
